# Fritzing sketch power management _ full (saved by Fritzing 0.9.10b)
breadboards: 1

parts:
  R1 = Resistor [tolerance=±5% resistance=120 package="0603 [SMD]"]
  R2 = TRIMPOT [maximum_resistance=1kΩ knob_status=50% power=0.5W package=trim_pot_pth]
  GND = Header 1 [package=1x01_offset]
  VIN = Header 1 [package=1x01_offset]
  D1 = Rectifier Diode 10A [part_number=1N4001]
  C2 = Capacitor Polarized [part_number=4.7uF package=panasonic_d]
  C1 = Capacitor Polarized [part_number=10uF package=panasonic_d]
  VOUT = Header 1 [package=1x01_offset]
  U1 = Voltage Regulator [package=to220-adj]
  D2 = Rectifier Diode 10A [part_number=1N4001]

nets:
  N1: R1.Pin_0, R2.CCW, C1.+, U1.ADJ, D2.anode
  N2: R1.Pin_1, D1.anode, C2.+, VOUT.1, U1.OUT, D2.cathode
  GND: R2.WIPER, R2.CW, GND.1, C2.-, C1.-
  N3: VIN.1, D1.cathode, U1.IN

notes:
  10uF
  4.7uF
