# Fritzing sketch power management _ simple (saved by Fritzing 0.9.10b)
breadboards: 1

parts:
  R1 = Resistor [tolerance=±5% resistance=120 package="0603 [SMD]"]
  R2 = TRIMPOT [maximum_resistance=1kΩ knob_status=50% power=0.5W package=trim_pot_pth]
  GND = Header 1 [package=1x01_offset]
  VIN = Header 1 [package=1x01_offset]
  VOUT = Header 1 [package=1x01_offset]
  U1 = Voltage Regulator [package=to220-adj]

nets:
  N1: R1.Pin_0, R2.CCW, U1.ADJ
  N2: R1.Pin_1, VOUT.1, U1.OUT
  GND: R2.WIPER, R2.CW, GND.1
  N3: VIN.1, U1.IN
