# Fritzing sketch power management (saved by Fritzing 0.9.10b)
breadboards: 1

parts:
  IC1 = Voltage Regulator [package=to-220-alt]
  R1 = Resistor [tolerance=±5% resistance=220 package="0603 [SMD]"]
  R2 = TRIMPOT [maximum_resistance=10kΩ knob_status=50% power=0.5W package=trim_pot_pth]
  U2 = Header 1 [package=1x01_offset]
  U3 = Header 1 [package=1x01_offset]

nets:
  N1: IC1.GND, R1.Pin_0, R2.CCW
  N2: IC1.IN, U3.1
  N3: IC1.OUT, R1.Pin_1
  N4: R2.CW, U2.1
